# Fritzing sketch robot (saved by Fritzing 0.9.3b)

parts:
  L1 = Solenoid
  L2 = Solenoid
  L3 = Solenoid
  L4 = Solenoid
  Part1 = Arduino Pro Mini v13
  IR_Detector = Photocell (LDR) [package=THT]
  IR_Emitter = LED - 5mm [color="Infrared (940nm)" package="5 mm [THT]"]
  R2 = Resistor [tolerance=±5% resistance=100 package=THT]
  R3 = Resistor [tolerance=±5% resistance=10k package=THT]
  VCC1 = Battery block 9V
  Part2 = Motor Driver 1A Dual TB6612FNG
  Motor_A_(Drive) = DC Motor
  Motor_B_(steering) = DC Motor
  Q1 = PNP-Transistor [package="SOT-23 [SMD]"]
  R4 = Resistor [tolerance=±5% resistance=1k package=THT]

nets:
  N1: L1.pin1, L2.pin1, L3.pin1, L4.pin1, Q1.1
  GND: L1.pin2, L2.pin2, L3.pin2, L4.pin2, Part1.GND, IR_Detector.pin_1, R2.Pin_1, VCC1.-, Part2.GND
  VCC: Part1.VCC, IR_Emitter.anode, R3.Pin_1, Part2.VCC, Part2.VM
  N2: Part1.RAW, VCC1.+, Q1.2
  N3: Part1.D10_PWM/SS, R4.Pin_0
  N4: Part1.D9_PWM, Part2.STBY
  N5: Part1.D8, Part2.BIN2
  N6: Part1.D7, Part2.BIN1
  N7: Part1.D6_PWM, Part2.PWMB
  N8: Part1.D5_PWM, Part2.PWMA
  N9: Part1.D4, Part2.AIN2
  N10: Part1.D3_PWM, IR_Detector.pin_0, R3.Pin_0
  N11: Part1.D2, Part2.AIN1
  N12: IR_Emitter.cathode, R2.Pin_0
  N13: Part2.B01, Motor_B_(steering).pin_1
  N14: Part2.B02, Motor_B_(steering).pin_2
  N15: Part2.A02, Motor_A_(Drive).pin_2
  N16: Part2.A01, Motor_A_(Drive).pin_1
  N17: Q1.0, R4.Pin_1
